// Logisim project Computer.circ as structural Verilog: 1 circuit, main circuit main
module main (
  output Stop_Lamp
);

  wire ADD, and_1_out, and_2_out, and_3_out, and_4_out, and_5_out, and_6_out, and_7_out, and_8_out,
       and_9_out, and_10_out, and_11_out, and_12_out, and_13_out, and_14_out, and_15_out, clk, DIV, HLT, JMP,
       JRP, LDN, MUL, or_2_out, or_3_out, or_5_out, or_6_out, or_7_out, s_r_ff_1_qn, SKN, STO, SUB, t0, t1,
       t2, t3, t4, t5, t6, t7;
  wire [0:0] comparator_1_lt;
  wire [2:0] CTR3_q;
  wire [15:0] adder_2_out, adder_3_out, adder_4_out, multiplexer_6_out, multiplexer_7_out, multiplexer_8_out,
       multiplexer_9_out, multiplexer_10_out, multiplexer_11_out, multiplexer_12_out, multiplexer_13_out,
       multiplexer_14_out, multiplexer_15_out, or_4_out, or_8_out, PC_q;
  wire [31:0] Acc_q, adder_1_out, divider_1_out, IR_q, multiplexer_1_out, multiplexer_2_out,
       multiplexer_3_out, multiplexer_4_out, multiplexer_5_out, multiplier_1_out, or_1_out, ram_1_dout,
       subtractor_1_out;

  Clock clock_1 (.out(clk));
  and and_1 (and_1_out, t4, LDN);
  Subtractor #(.width(32)) subtractor_1 (.a(Acc_q), .b(ram_1_dout), .out(subtractor_1_out));  // open: bin, bout
  Adder #(.width(32)) adder_1 (.a(Acc_q), .b(ram_1_dout), .out(adder_1_out));  // open: cin, cout
  Multiplier #(.width(32)) multiplier_1 (.a(Acc_q), .b(ram_1_dout), .out(multiplier_1_out));  // open: cin, cout
  Divider #(.width(32)) divider_1 (.a(Acc_q), .b(ram_1_dout), .out(divider_1_out));  // open: upper, rem
  and and_2 (and_2_out, HLT, t4);
  Multiplexer #(.width(32)) multiplexer_1 (
    .in0({32{1'b0}}), .in1(ram_1_dout), .out(multiplexer_1_out), .sel(and_1_out));
  S_R_Flip_Flop s_r_ff_1 (.S(and_2_out), .R(1'b0), .clk(clk), .Q(Stop_Lamp), .Qn(s_r_ff_1_qn));  // open: reset, preset
  Multiplexer #(.width(32)) multiplexer_2 (
    .in0({32{1'b0}}), .in1(subtractor_1_out), .out(multiplexer_2_out), .sel(and_3_out));
  and and_3 (and_3_out, t4, SUB);
  Multiplexer #(.width(32)) multiplexer_3 (
    .in0({32{1'b0}}), .in1(adder_1_out), .out(multiplexer_3_out), .sel(and_4_out));
  and and_4 (and_4_out, t4, ADD);
  Multiplexer #(.width(32)) multiplexer_4 (
    .in0({32{1'b0}}), .in1(multiplier_1_out), .out(multiplexer_4_out), .sel(and_5_out));
  and and_5 (and_5_out, t4, MUL);
  Multiplexer #(.width(32)) multiplexer_5 (
    .in0({32{1'b0}}), .in1(divider_1_out), .out(multiplexer_5_out), .sel(and_6_out));
  and and_6 (and_6_out, t4, DIV);
  Register #(.width(32)) IR (.D(ram_1_dout), .en(t2), .clk(clk), .Q(IR_q));  // open: clr
  and and_7 (and_7_out, clk, s_r_ff_1_qn);
  assign or_1_out = multiplexer_1_out | multiplexer_2_out | multiplexer_3_out | multiplexer_4_out | multiplexer_5_out;  // OR_Gate or_1, 32 bits wide
  or or_2 (or_2_out, and_1_out, and_3_out, and_4_out, and_5_out, and_6_out);
  Decoder #(.select(4)) decoder_1 (
    .out0(JMP), .out1(JRP), .out2(LDN), .out3(STO), .out4(SKN), .out5(SUB), .out6(ADD), .out7(MUL),
    .out8(DIV), .out9(HLT), .sel(IR_q[19:16]));  // open: out10, out11, out12, out13, out14, out15, en
  Counter #(.max('h5), .trigger("falling"), .width(3)) CTR3 (
    .clk(and_7_out), .Q(CTR3_q));  // open: clr, load, up, count, D, carry
  Register #(.width(32)) Acc (.D(or_1_out), .en(or_2_out), .clk(clk), .Q(Acc_q));  // open: clr
  Comparator #(.width(32)) comparator_1 (.a(Acc_q), .b({32{1'b0}}), .lt(comparator_1_lt[0]));  // open: gt, eq
  Decoder #(.select(3)) decoder_2 (
    .out0(t0), .out1(t1), .out2(t2), .out3(t3), .out4(t4), .out5(t5), .out6(t6), .out7(t7), .sel(CTR3_q));  // open: en
  Adder #(.width(16)) adder_2 (.a(ram_1_dout[15:0]), .b(PC_q), .out(adder_2_out));  // open: cin, cout
  Adder #(.width(16)) adder_3 (.a(16'h1), .b(PC_q), .out(adder_3_out));  // open: cin, cout
  Adder #(.width(16)) adder_4 (.a(PC_q), .b({{15{1'b0}}, comparator_1_lt[0]}), .out(adder_4_out));  // open: cin, cout
  or or_3 (or_3_out, STO, LDN, SUB, ADD, MUL, DIV);
  and and_8 (and_8_out, SKN, t5);
  and and_9 (and_9_out, JMP, t5);
  and and_10 (and_10_out, JRP, t5);
  and and_11 (and_11_out, or_3_out, t5);
  Multiplexer #(.width(16)) multiplexer_6 (.in0({16{1'b0}}), .in1(adder_3_out), .out(multiplexer_6_out), .sel(t0));
  Multiplexer #(.width(16)) multiplexer_7 (
    .in0({16{1'b0}}), .in1(adder_4_out), .out(multiplexer_7_out), .sel(and_8_out));
  Multiplexer #(.width(16)) multiplexer_8 (
    .in0({16{1'b0}}), .in1(ram_1_dout[15:0]), .out(multiplexer_8_out), .sel(and_9_out));
  Multiplexer #(.width(16)) multiplexer_9 (
    .in0({16{1'b0}}), .in1(adder_2_out), .out(multiplexer_9_out), .sel(and_10_out));
  Multiplexer #(.width(16)) multiplexer_10 (.in0({16{1'b0}}), .in1(PC_q), .out(multiplexer_10_out), .sel(and_11_out));
  assign or_4_out = multiplexer_6_out | multiplexer_7_out | multiplexer_8_out | multiplexer_9_out | multiplexer_10_out;  // OR_Gate or_4, 16 bits wide
  or or_5 (or_5_out, t0, t5);
  Register #(.width(16)) PC (.D(or_4_out), .en(or_5_out), .clk(clk), .Q(PC_q));  // open: clr
  or or_6 (or_6_out, SUB, ADD, MUL, DIV);
  or or_7 (or_7_out, JMP, JRP);
  and and_12 (and_12_out, t3, LDN);
  and and_13 (and_13_out, t3, STO);
  and and_14 (and_14_out, t3, or_6_out);
  Multiplexer #(.width(16)) multiplexer_11 (
    .in0({16{1'b0}}), .in1(IR_q[15:0]), .out(multiplexer_11_out), .sel(and_15_out));
  and and_15 (and_15_out, t4, or_7_out);
  Multiplexer #(.width(16)) multiplexer_12 (.in0({16{1'b0}}), .in1(PC_q), .out(multiplexer_12_out), .sel(t1));
  Multiplexer #(.width(16)) multiplexer_13 (
    .in0({16{1'b0}}), .in1(IR_q[15:0]), .out(multiplexer_13_out), .sel(and_12_out));
  Multiplexer #(.width(16)) multiplexer_14 (
    .in0({16{1'b0}}), .in1(IR_q[15:0]), .out(multiplexer_14_out), .sel(and_13_out));
  Multiplexer #(.width(16)) multiplexer_15 (
    .in0({16{1'b0}}), .in1(IR_q[15:0]), .out(multiplexer_15_out), .sel(and_14_out));
  assign or_8_out = multiplexer_12_out | multiplexer_13_out | multiplexer_14_out | multiplexer_15_out | multiplexer_11_out;  // OR_Gate or_8, 16 bits wide
  RAM #(.addrWidth(16), .dataWidth(32)) ram_1 (
    .addr(or_8_out), .we(and_13_out), .oe(1'b1), .clk(clk), .din(Acc_q), .dout(ram_1_dout));
endmodule
